// Logisim project andornot.circ as structural Verilog: 1 circuit, main circuit main
module main (
  input  a,
  input  b,
  input  c,
  input  d,
  output F
);

  wire and_1_out, and_2_out, and_3_out, not_1_out, not_2_out, not_3_out, not_4_out;

  not not_1 (not_1_out, a);
  not not_2 (not_2_out, b);
  not not_3 (not_3_out, c);
  not not_4 (not_4_out, d);
  and and_1 (and_1_out, a, not_2_out, d);
  and and_2 (and_2_out, not_1_out, not_4_out);
  and and_3 (and_3_out, not_2_out, not_3_out);
  or or_1 (F, and_1_out, and_2_out, and_3_out);
endmodule
