// Logisim project muxnot.circ as structural Verilog: 1 circuit, main circuit main
module main (
  input  _0___1,
  input  enable,
  input  [2:0] a_b_c,
  input  d,
  output F
);

  wire not_1_out, not_2_out;

  not not_1 (not_1_out, _0___1);
  not not_2 (not_2_out, d);
  Multiplexer #(.select(3)) multiplexer_1 (
    .in0(not_1_out), .in1(not_2_out), .in2(not_2_out), .in3(not_2_out), .in4(not_1_out), .in5(d),
    .in6(_0___1), .in7(_0___1), .out(F), .sel(a_b_c), .en(enable));
endmodule
