// Logisim project addersubtracter.circ as structural Verilog: 1 circuit, main circuit main
module main (
  input  Add_Subtract,
  input  B0,
  input  B1,
  input  B2,
  input  B3,
  input  A0,
  input  A1,
  input  A2,
  input  A3,
  output C0,
  output C1,
  output C2,
  output C3,
  output Cout
);

  wire [3:0] xor_1_out;

  xor xor_1 (xor_1_out[0], B0, Add_Subtract);
  xor xor_2 (xor_1_out[1], B1, Add_Subtract);
  xor xor_3 (xor_1_out[2], B2, Add_Subtract);
  xor xor_4 (xor_1_out[3], B3, Add_Subtract);
  Adder #(.width(4)) adder_1 (
    .a(xor_1_out), .b({A3, A2, A1, A0}), .out({C3, C2, C1, C0}), .cin(Add_Subtract), .cout(Cout));
endmodule
