// Logisim project counter.circ as structural Verilog: 1 circuit, main circuit main
module main (
  input  in_1,
  input  in_2,
  input  in_3,
  input  P0,
  input  P1,
  input  P2,
  input  P3,
  input  in_8,
  output out_9,
  output out_10,
  output out_11,
  output out_12,
  output out_13
);

  wire _7_segment_display_divider_p5, _7_segment_display_divider_p6, _7_segment_display_divider_p7,
       _7_segment_display_divider_p8, _7_segment_display_divider_p9, _7_segment_display_divider_p10,
       _7_segment_display_divider_p11, clock_1_out, ic_74161_1_p8, not_1_out, not_2_out;

  Clock clock_1 (.out(clock_1_out));
  // IC_74161 ic_74161_1: pin names not known; wires that end beside it: P0, P1, P2, P3, clock_1_out, in_3, in_2, ic_74161_1_p8, in_1, out_9, out_10, out_11, out_12, out_13
  nand nand_1 (ic_74161_1_p8, not_1_out, out_10, out_11, not_2_out);
  not not_1 (not_1_out, out_9);
  not not_2 (not_2_out, out_12);
  // _7_segment_display_driver _7_segment_display_divider: pin names not known; wires that end beside it: out_12, out_11, out_10, out_9, _7_segment_display_divider_p5, _7_segment_display_divider_p6, _7_segment_display_divider_p7, _7_segment_display_divider_p8, _7_segment_display_divider_p9, _7_segment_display_divider_p10, _7_segment_display_divider_p11
  _7_Segment_Display u_7_segment_display_1 (
    .g(_7_segment_display_divider_p11), .f(_7_segment_display_divider_p10),
    .a(_7_segment_display_divider_p5), .b(_7_segment_display_divider_p6), .e(_7_segment_display_divider_p9),
    .d(_7_segment_display_divider_p8), .c(_7_segment_display_divider_p7), .dp(in_8));

  // Notes on the sheet:
  //   PE(low)
  //   CEP
  //   SR(low)
  //   CP
  //   CET
  //   TC
  //   Q0
  //   Q1
  //   Q2
  //   Q3
endmodule
