// Logisim project d_flip_flop.circ as structural Verilog: 2 circuits, main circuit main
module main (
  input  D,
  output Q,
  output Qn
);

  wire clock_out, D_Latch_1_q, D_Latch_1_qn, not_1_out;

  Clock clock (.out(clock_out));
  d_latch D_Latch_1 (.D(D), .E(clock_out), .Q(D_Latch_1_q), .Qn(D_Latch_1_qn));
  not not_1 (not_1_out, clock_out);
  d_latch D_Latch_2 (.D(D_Latch_1_q), .E(not_1_out), .Q(Q), .Qn(Qn));

  // Notes on the sheet:
  //   D
  //   E
  //   Q
  //   Qn
  //   Q
  //   D
  //   Qn
  //   E
endmodule

module d_latch (
  input  D,
  input  E,
  output Q,
  output Qn
);

  wire nand_1_out, nand_2_out, nand_3_out;

  nand nand_1 (nand_1_out, D, D);
  nand nand_2 (nand_2_out, D, E);
  nand nand_3 (nand_3_out, E, nand_1_out);
  nand nand_4 (Q, nand_2_out, Qn);
  nand nand_5 (Qn, Q, nand_3_out);
endmodule
