// Logisim project pulse_generator.circ as structural Verilog: 1 circuit, main circuit main
module main (
  input  [7:0] in_1,
  input  in_2,
  input  en,
  input  clr,
  output out_5,
  output out_6
);

  wire _74165_pin1, _74165_pin8, _74165_pin16, clock_1_out;

  Clock clock_1 (.out(clock_1_out));
  _74165 #(.VccGndPorts("true"), .ShowInternalStructure("true")) _74165 (
    .pin1(_74165_pin1), .pin2(clock_1_out), .pin3(in_1[4]), .pin4(in_1[5]), .pin5(in_1[6]), .pin6(in_1[7]),
    .pin7(out_6), .pin8(_74165_pin8), .pin16(_74165_pin16), .pin15(_74165_pin8), .pin14(in_1[3]),
    .pin13(in_1[2]), .pin12(in_1[1]), .pin11(in_1[0]), .pin10(out_5), .pin9(out_5));
  Multiplexer #(.enable("false")) multiplexer_1 (.in0(_74165_pin8), .in1(_74165_pin16), .out(_74165_pin1), .sel(in_2));
  // Digital_Oscilloscope digital_oscilloscope_1: pin names not known; wires that end beside it: clock_1_out, out_5, out_6, en, clr
  // also tied to GND on the sheet: _74165_pin8
  // also tied to VCC on the sheet: _74165_pin16

  // Notes on the sheet:
  //   clock
  //   Q
  //   Qn
endmodule
