// Logisim project sr_latch_w_en.circ as structural Verilog: 1 circuit, main circuit main
module main (
  input  S,
  input  E,
  input  R,
  output Q,
  output Qn
);

  wire nand_1_out, nand_2_out;

  nand nand_1 (nand_1_out, S, E);
  nand nand_2 (nand_2_out, E, R);
  nand nand_3 (Q, nand_1_out, Qn);
  nand nand_4 (Qn, Q, nand_2_out);
endmodule
