// Logisim project sr_latch_wo_en.circ as structural Verilog: 1 circuit, main circuit main
module main (
  input  S,
  input  R,
  output Qn,
  output Q
);

  nor nor_1 (Qn, S, Q);
  nor nor_2 (Q, Qn, R);
endmodule
